# Fritzing sketch SKEMATIC WIMS FRITZING (saved by Fritzing 0.9.4)

parts:
  Part1 = Arduino Nano (Rev3.0) (ICSP)
  Part2 = LCD1602-I2C
  S1 = Momentary Switch [package=ksa_sealed_tac_switch]
  S2 = Momentary Switch [package=ksa_sealed_tac_switch]
  S3 = Momentary Switch [package=ksa_sealed_tac_switch]
  S4 = Momentary Switch [package=ksa_sealed_tac_switch]
  POWER_SUPLAY_12_V = Jtron 1 Channel Optoisolated Relay Module [package=relay]
  part = DC Motor

nets:
  GND: Part1.GND, Part1.RESET, Part2.GND, S1.1
  N1: Part1.D8, POWER_SUPLAY_12_V.IN1
  VIN: Part1.VIN, Part2.VCC
  N2: Part1.A5, Part2.SCL
  N3: Part1.A4, Part1.A3, Part2.SDA, S1.3
  N4: Part1.A2, S2.3
  N5: Part1.A1, S3.3
  N6: Part1.A0, S4.3
  N7: POWER_SUPLAY_12_V.NC, part.pin_1

custom parts:
  LCD1602-I2C: A standard character display, usually with 2x16 characters. Comes in many colors with LCM1602 IIC attached.
